// Logisim project cpu.circ as structural Verilog: 6 circuits, main circuit main
module main (
);

  wire Add, AddI, And, and_1_out, Beq, Clock, Jump, Load, Mult, not_1_out, not_2_out, not_3_out, not_4_out,
       Or, Reset_out, Store, Sub, Tipo_R;
  wire [1:0] controlled_buffer_4_out_5;
  wire [3:0] bit_extender_1_out, bit_extender_2_out, bit_extender_3_out, bit_extender_4_out,
       controlled_buffer_1_out, controlled_buffer_4_out_2, controlled_buffer_4_out_3,
       controlled_buffer_4_out_4, controlled_buffer_5_out, controlled_buffer_5_out_2,
       controlled_buffer_5_out_3, controlled_buffer_5_out_4, controlled_buffer_6_out_2,
       controlled_buffer_6_out_3, controlled_buffer_6_out_4, controlled_buffer_6_out_5,
       controlled_buffer_6_out_6, controlled_buffer_7_out, controlled_buffer_7_out_2,
       controlled_buffer_7_out_3, controlled_buffer_7_out_4, controlled_buffer_7_out_5,
       controlled_buffer_7_out_6, controlled_buffer_7_out_7, controlled_buffer_7_out_8,
       controlled_buffer_8_out_2, controlled_buffer_8_out_3, controlled_buffer_8_out_4,
       controlled_buffer_8_out_5, controlled_buffer_8_out_6;
  wire [4:0] controlled_buffer_2_out, controlled_buffer_3_out, Rd, Rs, Rt;
  wire [4:4] controlled_buffer_1_out_2;
  wire [11:0] controlled_buffer_4_out, controlled_buffer_6_out, controlled_buffer_8_out;
  wire [15:0] Address;
  wire [25:0] JAddress;
  wire [27:0] Data;
  wire [31:0] pc_1_data, RdOut, RsOut, RtOut;

  Button Reset (.out(Reset_out));
  Clock clock_1 (.out(Clock));
  _7_Segment_Display u_7_segment_display_1 (
    .g(Data[24]), .f(Data[23]), .a(Data[22]), .b(Data[21]), .e(Data[25]), .d(Data[26]), .c(Data[27]));  // open: dp
  _7_Segment_Display u_7_segment_display_2 (
    .g(Data[17]), .f(Data[16]), .a(Data[15]), .b(Data[14]), .e(Data[18]), .d(Data[19]), .c(Data[20]));  // open: dp
  pc pc_1 (.clk(Clock), .reset(Reset_out), .data(pc_1_data));
  Multiplexer #(.width(28), .disabled(0), .enable("false")) multiplexer_1 (
    .in1(28'hbfe7c80), .out(Data), .sel(Add));  // open: in0
  Multiplexer #(.width(28), .disabled(0), .enable("false")) multiplexer_2 (
    .in1(28'hf9d7700), .out(Data), .sel(Sub));  // open: in0
  Multiplexer #(.width(28), .disabled(0), .enable("false")) multiplexer_3 (
    .in1(28'hbf5fc80), .out(Data), .sel(And));  // open: in0
  Multiplexer #(.width(28), .disabled(0), .enable("false")) multiplexer_4 (
    .in1(28'hee58000), .out(Data), .sel(Or));  // open: in0
  Multiplexer #(.width(28), .disabled(0), .enable("false")) multiplexer_5 (
    .in1(28'hb5d5a3c), .out(Data), .sel(Mult));  // open: in0
  Multiplexer #(.width(28), .disabled(0), .enable("false")) multiplexer_6 (
    .in1(28'hf8fe780), .out(Data), .sel(Beq));  // open: in0
  _7_Segment_Display u_7_segment_display_3 (
    .g(Data[10]), .f(Data[9]), .a(Data[8]), .b(Data[7]), .e(Data[11]), .d(Data[12]), .c(Data[13]));  // open: dp
  decoder decoder_1 (
    .Address(pc_1_data), .Tipo_R(Tipo_R), .Address_2(Address), .Rd(Rd), .Rt(Rt), .Rs(Rs),
    .JAddress(JAddress), .Add(Add), .Sub(Sub), .And(And), .Or(Or), .Mult(Mult), .Beq(Beq), .AddI(AddI),
    .Load(Load), .Store(Store), .Jump(Jump));
  _7_Segment_Display u_7_segment_display_4 (
    .g(Data[3]), .f(Data[2]), .a(Data[1]), .b(Data[0]), .e(Data[4]), .d(Data[5]), .c(Data[6]));  // open: dp
  Multiplexer #(.width(28), .disabled(0), .enable("false")) multiplexer_7 (
    .in1(28'hbfe7c94), .out(Data), .sel(AddI));  // open: in0
  Multiplexer #(.width(28), .disabled(0), .enable("false")) multiplexer_8 (
    .in1(28'h69deff9), .out(Data), .sel(Load));  // open: in0
  Multiplexer #(.width(28), .disabled(0), .enable("false")) multiplexer_9 (
    .in1(28'hdcf0000), .out(Data), .sel(Store));  // open: in0
  Multiplexer #(.width(28), .disabled(0), .enable("false")) multiplexer_10 (
    .in1(28'hc3d6d1f), .out(Data), .sel(Jump));  // open: in0
  Hex_Digit_Display hex_digit_display_1 (.value(bit_extender_2_out));  // open: dp
  assign {controlled_buffer_1_out_2[4], controlled_buffer_1_out} = not_1_out ? Rs : 5'bz;  // Controlled_Buffer controlled_buffer_1
  not not_1 (not_1_out, Jump);
  Hex_Digit_Display hex_digit_display_2 (.value(bit_extender_1_out));  // open: dp
  assign bit_extender_1_out = {{2{1'b0}}, controlled_buffer_4_out_5};  // Bit_Extender bit_extender_1
  Hex_Digit_Display hex_digit_display_3 (.value(controlled_buffer_1_out));  // open: dp
  assign bit_extender_2_out = {{3{1'b0}}, controlled_buffer_1_out_2[4]};  // Bit_Extender bit_extender_2
  assign controlled_buffer_2_out = not_2_out ? Rt : 5'bz;  // Controlled_Buffer controlled_buffer_2
  not not_2 (not_2_out, Jump);
  Hex_Digit_Display hex_digit_display_4 (.value(controlled_buffer_4_out_4));  // open: dp
  registers registers_1 (.Rs(Rs), .Rt(Rt), .Rd(Rd), .Clock(Clock), .RsOut(RsOut), .RtOut(RtOut), .RdOut(RdOut));
  Hex_Digit_Display hex_digit_display_5 (.value(bit_extender_3_out));  // open: dp
  assign bit_extender_3_out = {{3{1'b0}}, controlled_buffer_2_out[4]};  // Bit_Extender bit_extender_3
  Hex_Digit_Display hex_digit_display_6 (.value(controlled_buffer_4_out_3));  // open: dp
  Hex_Digit_Display hex_digit_display_7 (.value(controlled_buffer_2_out[3:0]));  // open: dp
  Hex_Digit_Display hex_digit_display_8 (.value(bit_extender_4_out));  // open: dp
  assign controlled_buffer_3_out = Tipo_R ? Rd : 5'bz;  // Controlled_Buffer controlled_buffer_3
  Hex_Digit_Display hex_digit_display_9 (.value(controlled_buffer_4_out_2));  // open: dp
  Hex_Digit_Display hex_digit_display_10 (.value(controlled_buffer_4_out[11:8]));  // open: dp
  assign {controlled_buffer_4_out_5, controlled_buffer_4_out_4, controlled_buffer_4_out_3, controlled_buffer_4_out_2, controlled_buffer_4_out} = Jump ? JAddress : 26'bz;  // Controlled_Buffer controlled_buffer_4
  Hex_Digit_Display hex_digit_display_11 (.value(controlled_buffer_3_out[3:0]));  // open: dp
  assign bit_extender_4_out = {{3{1'b0}}, controlled_buffer_3_out[4]};  // Bit_Extender bit_extender_4
  Hex_Digit_Display hex_digit_display_12 (.value(controlled_buffer_4_out[7:4]));  // open: dp
  Hex_Digit_Display hex_digit_display_13 (.value(controlled_buffer_6_out_6));  // open: dp
  Hex_Digit_Display hex_digit_display_14 (.value(controlled_buffer_7_out_8));  // open: dp
  Hex_Digit_Display hex_digit_display_15 (.value(controlled_buffer_5_out_4));  // open: dp
  Hex_Digit_Display hex_digit_display_16 (.value(controlled_buffer_4_out[3:0]));  // open: dp
  Hex_Digit_Display hex_digit_display_17 (.value(controlled_buffer_6_out_5));  // open: dp
  Hex_Digit_Display hex_digit_display_18 (.value(controlled_buffer_7_out_7));  // open: dp
  Hex_Digit_Display hex_digit_display_19 (.value(controlled_buffer_5_out_3));  // open: dp
  Hex_Digit_Display hex_digit_display_20 (.value(controlled_buffer_5_out_2));  // open: dp
  assign {controlled_buffer_5_out_4, controlled_buffer_5_out_3, controlled_buffer_5_out_2, controlled_buffer_5_out} = and_1_out ? Address : 16'bz;  // Controlled_Buffer controlled_buffer_5
  not not_3 (not_3_out, Tipo_R);
  not not_4 (not_4_out, Jump);
  Hex_Digit_Display hex_digit_display_21 (.value(controlled_buffer_6_out_4));  // open: dp
  Hex_Digit_Display hex_digit_display_22 (.value(controlled_buffer_6_out_3));  // open: dp
  Hex_Digit_Display hex_digit_display_23 (.value(controlled_buffer_7_out_6));  // open: dp
  Hex_Digit_Display hex_digit_display_24 (.value(controlled_buffer_5_out));  // open: dp
  and and_1 (and_1_out, not_3_out, not_4_out);
  Hex_Digit_Display hex_digit_display_25 (.value(controlled_buffer_6_out_2));  // open: dp
  assign {controlled_buffer_6_out_6, controlled_buffer_6_out_5, controlled_buffer_6_out_4, controlled_buffer_6_out_3, controlled_buffer_6_out_2, controlled_buffer_6_out} = Tipo_R ? RsOut : 32'bz;  // Controlled_Buffer controlled_buffer_6
  Hex_Digit_Display hex_digit_display_26 (.value(controlled_buffer_7_out_4));  // open: dp
  Hex_Digit_Display hex_digit_display_27 (.value(controlled_buffer_7_out_5));  // open: dp
  Hex_Digit_Display hex_digit_display_28 (.value(controlled_buffer_6_out[11:8]));  // open: dp
  Hex_Digit_Display hex_digit_display_29 (.value(controlled_buffer_7_out_3));  // open: dp
  assign {controlled_buffer_7_out_8, controlled_buffer_7_out_7, controlled_buffer_7_out_6, controlled_buffer_7_out_5, controlled_buffer_7_out_4, controlled_buffer_7_out_3, controlled_buffer_7_out_2, controlled_buffer_7_out} = Tipo_R ? RtOut : 32'bz;  // Controlled_Buffer controlled_buffer_7
  Hex_Digit_Display hex_digit_display_30 (.value(controlled_buffer_6_out[7:4]));  // open: dp
  Hex_Digit_Display hex_digit_display_31 (.value(controlled_buffer_6_out[3:0]));  // open: dp
  Hex_Digit_Display hex_digit_display_32 (.value(controlled_buffer_7_out_2));  // open: dp
  Hex_Digit_Display hex_digit_display_33 (.value(controlled_buffer_8_out_6));  // open: dp
  Hex_Digit_Display hex_digit_display_34 (.value(controlled_buffer_7_out));  // open: dp
  Hex_Digit_Display hex_digit_display_35 (.value(controlled_buffer_8_out_5));  // open: dp
  Hex_Digit_Display hex_digit_display_36 (.value(controlled_buffer_8_out_3));  // open: dp
  Hex_Digit_Display hex_digit_display_37 (.value(controlled_buffer_8_out_4));  // open: dp
  Hex_Digit_Display hex_digit_display_38 (.value(controlled_buffer_8_out_2));  // open: dp
  assign {controlled_buffer_8_out_6, controlled_buffer_8_out_5, controlled_buffer_8_out_4, controlled_buffer_8_out_3, controlled_buffer_8_out_2, controlled_buffer_8_out} = Tipo_R ? RdOut : 32'bz;  // Controlled_Buffer controlled_buffer_8
  Hex_Digit_Display hex_digit_display_39 (.value(controlled_buffer_8_out[11:8]));  // open: dp
  Hex_Digit_Display hex_digit_display_40 (.value(controlled_buffer_8_out[3:0]));  // open: dp
  Hex_Digit_Display hex_digit_display_41 (.value(controlled_buffer_8_out[7:4]));  // open: dp

  // Notes on the sheet:
  //   Decoder
  //   Instruction
  //   rs
  //   rt
  //   Jump Address
  //   rd
  //   Address
  //   Rs Info
  //   Rt Info
  //   Rd Info
endmodule

module decoder (
  input  [31:0] Address,
  output Tipo_R,
  output [15:0] Address_2,
  output [4:0] Rd,
  output [4:0] Rt,
  output [4:0] Rs,
  output [25:0] JAddress,
  output Add,
  output Sub,
  output And,
  output Or,
  output Mult,
  output Beq,
  output AddI,
  output Load,
  output Store,
  output Jump
);

  wire comparator_1_eq, comparator_2_eq, comparator_3_eq, comparator_5_eq, comparator_6_eq, comparator_7_eq,
       comparator_8_eq, comparator_9_eq, comparator_10_eq, comparator_11_eq, not_1_out, not_2_out, not_3_out,
       not_4_out, not_5_out;

  Comparator #(.width(6)) comparator_1 (.a(Address[5:0]), .b(6'b100000), .eq(comparator_1_eq));  // open: gt, lt
  not not_1 (not_1_out, Tipo_R);
  Comparator #(.width(6)) comparator_2 (.a(Address[31:26]), .b(6'b000100), .eq(comparator_2_eq));  // open: gt, lt
  not not_2 (not_2_out, Tipo_R);
  Comparator #(.width(6)) comparator_3 (.a(Address[31:26]), .b(6'b000010), .eq(comparator_3_eq));  // open: gt, lt
  and and_1 (Add, Tipo_R, comparator_1_eq);
  and and_2 (Beq, not_1_out, comparator_2_eq);
  and and_3 (Jump, not_2_out, comparator_3_eq);
  Comparator #(.width(6)) comparator_4 (.a(Address[31:26]), .b({6{1'b0}}), .eq(Tipo_R));  // open: gt, lt
  Comparator #(.width(6)) comparator_5 (.a(Address[5:0]), .b(6'b100010), .eq(comparator_5_eq));  // open: gt, lt
  Comparator #(.width(6)) comparator_6 (.a(Address[31:26]), .b(6'b001000), .eq(comparator_6_eq));  // open: gt, lt
  and and_4 (Sub, Tipo_R, comparator_5_eq);
  not not_3 (not_3_out, Tipo_R);
  and and_5 (AddI, not_3_out, comparator_6_eq);
  Comparator #(.width(6)) comparator_7 (.a(Address[5:0]), .b(6'b100100), .eq(comparator_7_eq));  // open: gt, lt
  and and_6 (And, Tipo_R, comparator_7_eq);
  not not_4 (not_4_out, Tipo_R);
  Comparator #(.width(6)) comparator_8 (.a(Address[31:26]), .b(6'b100011), .eq(comparator_8_eq));  // open: gt, lt
  and and_7 (Load, not_4_out, comparator_8_eq);
  Comparator #(.width(6)) comparator_9 (.a(Address[5:0]), .b(6'b100101), .eq(comparator_9_eq));  // open: gt, lt
  Comparator #(.width(6)) comparator_10 (.a(Address[31:26]), .b(6'b101011), .eq(comparator_10_eq));  // open: gt, lt
  and and_8 (Or, Tipo_R, comparator_9_eq);
  not not_5 (not_5_out, Tipo_R);
  and and_9 (Store, not_5_out, comparator_10_eq);
  Comparator #(.width(6)) comparator_11 (.a(Address[5:0]), .b(6'b011000), .eq(comparator_11_eq));  // open: gt, lt
  and and_10 (Mult, Tipo_R, comparator_11_eq);

  assign Address_2 = Address[15:0];
  assign JAddress = Address[25:0];
  assign Rd = Address[15:11];
  assign Rs = Address[25:21];
  assign Rt = Address[20:16];

  // Other names for the same wires on the sheet: Funct[5:0] = Address[5:0]; OpCode[5:0] = Address[31:26]
endmodule

module pc (
  input  clk,
  input  reset,
  output [31:0] data
);

  wire [7:0] register_1_q_2;
  wire [23:0] register_1_q;
  wire [31:0] adder_1_out;

  Register #(.width(32)) register_1 (
    .D(adder_1_out), .Q({register_1_q_2, register_1_q}), .clk(clk), .clr(reset));  // open: en
  Adder #(.width(32)) adder_1 (.a(32'h1), .b({register_1_q_2, register_1_q}), .out(adder_1_out));  // open: cin, cout
  ROM rom_1 (.pos(register_1_q), .data(data));  // open: sel
endmodule

module RAM (
  input  [23:0] pos,
  input  [31:0] data,
  input  sel,
  input  clk,
  input  ld,
  input  clr
);

  RAM_part #(.addrWidth(24), .dataWidth(32)) ram_1 (.addr(pos), .data(data), .sel(sel), .clk(clk), .ld(ld), .clr(clr));
endmodule

module ROM (
  input  [23:0] pos,
  input  sel,
  output [31:0] data
);

  ROM_part #(.addrWidth(24), .dataWidth(32)) rom_1 (.addr(pos), .data(data), .sel(sel));

  // Notes on the sheet:
  //   contents of rom_1 (hex, n*v repeats v):
  //   12c6820 11a00001 1a90020 8c890001 1397020 8100008 120c820 329c824 13200001 810000c 20 1019fff7
  //   1495020
endmodule

module registers (
  input  [4:0] Rs,
  input  [4:0] Rt,
  input  [4:0] Rd,
  input  Clock,
  output [31:0] RsOut,
  output [31:0] RtOut,
  output [31:0] RdOut
);

  wire [31:0] R0, R1, R2, R3, R4, R5, R6, R7, R8, R9, R10, R11, R12, R13, R14, R15, R16, R17, R18, R19, R20,
       R21, R22, R23, R24, R25, R26, R27, R28, R29, R30, R31;

  Register #(.width(32)) register_1 (.Q(R0), .clk(Clock));  // open: D, en, clr
  Register #(.width(32)) register_2 (.Q(R1), .clk(Clock));  // open: D, en, clr
  Register #(.width(32)) register_3 (.Q(R2), .clk(Clock));  // open: D, en, clr
  Register #(.width(32)) register_4 (.Q(R3), .clk(Clock));  // open: D, en, clr
  Register #(.width(32)) register_5 (.Q(R4), .clk(Clock));  // open: D, en, clr
  Register #(.width(32)) register_6 (.Q(R5), .clk(Clock));  // open: D, en, clr
  Register #(.width(32)) register_7 (.Q(R6), .clk(Clock));  // open: D, en, clr
  Register #(.width(32)) register_8 (.Q(R7), .clk(Clock));  // open: D, en, clr
  Register #(.width(32)) register_9 (.Q(R8), .clk(Clock));  // open: D, en, clr
  Register #(.width(32)) register_10 (.Q(R9), .clk(Clock));  // open: D, en, clr
  Register #(.width(32)) register_11 (.Q(R10), .clk(Clock));  // open: D, en, clr
  Register #(.width(32)) register_12 (.Q(R11), .clk(Clock));  // open: D, en, clr
  Register #(.width(32)) register_13 (.Q(R12), .clk(Clock));  // open: D, en, clr
  Register #(.width(32)) register_14 (.Q(R13), .clk(Clock));  // open: D, en, clr
  Register #(.width(32)) register_15 (.Q(R14), .clk(Clock));  // open: D, en, clr
  Register #(.width(32)) register_16 (.Q(R15), .clk(Clock));  // open: D, en, clr
  Register #(.width(32)) register_17 (.Q(R16), .clk(Clock));  // open: D, en, clr
  Register #(.width(32)) register_18 (.Q(R17), .clk(Clock));  // open: D, en, clr
  Register #(.width(32)) register_19 (.Q(R18), .clk(Clock));  // open: D, en, clr
  Register #(.width(32)) register_20 (.Q(R19), .clk(Clock));  // open: D, en, clr
  Register #(.width(32)) register_21 (.Q(R20), .clk(Clock));  // open: D, en, clr
  Register #(.width(32)) register_22 (.Q(R21), .clk(Clock));  // open: D, en, clr
  Register #(.width(32)) register_23 (.Q(R22), .clk(Clock));  // open: D, en, clr
  Register #(.width(32)) register_24 (.Q(R23), .clk(Clock));  // open: D, en, clr
  Register #(.width(32)) register_25 (.Q(R24), .clk(Clock));  // open: D, en, clr
  Register #(.width(32)) register_26 (.Q(R25), .clk(Clock));  // open: D, en, clr
  Register #(.width(32)) register_27 (.Q(R26), .clk(Clock));  // open: D, en, clr
  Register #(.width(32)) register_28 (.Q(R27), .clk(Clock));  // open: D, en, clr
  Register #(.width(32)) register_29 (.Q(R28), .clk(Clock));  // open: D, en, clr
  Register #(.width(32)) register_30 (.Q(R29), .clk(Clock));  // open: D, en, clr
  Register #(.width(32)) register_31 (.Q(R30), .clk(Clock));  // open: D, en, clr
  Register #(.width(32)) register_32 (.Q(R31), .clk(Clock));  // open: D, en, clr
  Multiplexer #(.select(5), .width(32), .enable("false")) multiplexer_1 (
    .in0(R0), .in1(R1), .in2(R2), .in3(R3), .in4(R4), .in5(R5), .in6(R6), .in7(R7), .in8(R8), .in9(R9),
    .in10(R10), .in11(R11), .in12(R12), .in13(R13), .in14(R14), .in15(R15), .in16(R16), .in17(R17),
    .in18(R18), .in19(R19), .in20(R20), .in21(R21), .in22(R22), .in23(R23), .in24(R24), .in25(R25),
    .in26(R26), .in27(R27), .in28(R28), .in29(R29), .in30(R30), .in31(R31), .out(RsOut), .sel(Rs));
  Multiplexer #(.select(5), .width(32), .enable("false")) multiplexer_2 (
    .in0(R0), .in1(R1), .in2(R2), .in3(R3), .in4(R4), .in5(R5), .in6(R6), .in7(R7), .in8(R8), .in9(R9),
    .in10(R10), .in11(R11), .in12(R12), .in13(R13), .in14(R14), .in15(R15), .in16(R16), .in17(R17),
    .in18(R18), .in19(R19), .in20(R20), .in21(R21), .in22(R22), .in23(R23), .in24(R24), .in25(R25),
    .in26(R26), .in27(R27), .in28(R28), .in29(R29), .in30(R30), .in31(R31), .out(RtOut), .sel(Rt));
  Multiplexer #(.select(5), .width(32), .enable("false")) multiplexer_3 (
    .in0(R0), .in1(R1), .in2(R2), .in3(R3), .in4(R4), .in5(R5), .in6(R6), .in7(R7), .in8(R8), .in9(R9),
    .in10(R10), .in11(R11), .in12(R12), .in13(R13), .in14(R14), .in15(R15), .in16(R16), .in17(R17),
    .in18(R18), .in19(R19), .in20(R20), .in21(R21), .in22(R22), .in23(R23), .in24(R24), .in25(R25),
    .in26(R26), .in27(R27), .in28(R28), .in29(R29), .in30(R30), .in31(R31), .out(RdOut), .sel(Rd));
endmodule
